// Logisim project Oscar.circ as structural Verilog
module Fetch (
  input  Clock,
  output [31:0] PC,
  output [31:0] Instruction
);

  wire [29:0] incrementer_1_p2;

  Register #(.width(32)) register_1 (.D({incrementer_1_p2, PC[1:0]}), .clk(Clock), .Q(PC));  // open: en, clr
  // Incrementer #(.width(30)) incrementer_1: pin names not known; wires that end beside it: PC[31:2], incrementer_1_p2, PC
  // RISC_VProgramROM risc_vprogramrom_1: pin names not known; wires that end beside it: Instruction
endmodule
