// Logisim project P2.circ as structural Verilog
module RISCV (
);

  wire Clk_out, decode_1_alustuffout, decode_1_f3lsb, decode_1_luiout, decode_1_opmout, decode_1_opxout,
       decode_1_registerout, decode_1_rtype, decode_1_uiout, execute_1_regwriteout,
       executeregister_1_regwriteout, memory_1_regwriteout;
  wire [3:0] decode_1_aluopout;
  wire [4:0] decode_1_rd, decode_1_rs1, decode_1_rs2, execute_1_rwout, executeregister_1_rwout,
       memory_1_rwout;
  wire [19:0] decode_1_immutype;
  wire [31:0] decode_1_aout, decode_1_bout, decode_1_immextended, decode_1_pcout, execute_1_aluoutput,
       execute_1_pcout, executeregister_1_alures_out, executeregister_1_pcout, fetch_1_instruction,
       fetch_1_pc, fetchregister_1_instructionout, fetchregister_1_pcout, memory_1_alures_out, memory_1_pcout;

  Clock Clk (.out(Clk_out));
  Fetch fetch_1 (.Clock(Clk_out), .PC(fetch_1_pc), .Instruction(fetch_1_instruction));
  FetchRegister fetchregister_1 (
    .PCIn(fetch_1_pc), .InstructionIn(fetch_1_instruction), .Clock(Clk_out), .PCOut(fetchregister_1_pcout),
    .InstructionOut(fetchregister_1_instructionout));
  Decode decode_1 (
    .InstructionIn(fetchregister_1_instructionout), .Clock(Clk_out), .PCIn(fetchregister_1_pcout),
    .OpXOut(decode_1_opxout), .OpMOut(decode_1_opmout), .ALUStuffOut(decode_1_alustuffout),
    .RegisterOut(decode_1_registerout), .RType(decode_1_rtype), .LUIOut(decode_1_luiout),
    .UIOut(decode_1_uiout), .RD(decode_1_rd), .f3LSB(decode_1_f3lsb), .ALUOpOut(decode_1_aluopout),
    .RS1(decode_1_rs1), .RS2(decode_1_rs2), .ImmExtended(decode_1_immextended), .ImmUType(decode_1_immutype),
    .AOut(decode_1_aout), .BOut(decode_1_bout), .PCOut(decode_1_pcout));  // open: WriteBack, RegisterWE, RegisterxW
  DecodeRegister decoderegister_1 (
    .OpXIn(decode_1_opxout), .OpMIn(decode_1_opmout), .ALUStuffIn(decode_1_alustuffout),
    .RegisterIn(decode_1_registerout), .RTypeIn(decode_1_rtype), .LUIIn(decode_1_luiout),
    .UIIn(decode_1_uiout), .RDIn(decode_1_rd), .f3LSBIn(decode_1_f3lsb), .ALUOpIn(decode_1_aluopout),
    .RS1In(decode_1_rs1), .RS2In(decode_1_rs2), .ImmExtendedIn(decode_1_immextended),
    .ImmUTypeIn(decode_1_immutype), .AIn(decode_1_aout), .BIn(decode_1_bout), .PCIn(decode_1_pcout),
    .Clock(Clk_out));  // open: OpXOut, OpMOut, ALUStuffOut, RegisterOut, RTypeOut, LUIOut, UIOut, RDOut, f3LSBOut, ALUOpOut, RS1Out, RS2Out, ImmExtendedOut, ImmUTypeOut, AOut, BOut, PCOut
  Execute execute_1 (
    .ALUOutput(execute_1_aluoutput), .RegWriteOut(execute_1_regwriteout), .rWout(execute_1_rwout),
    .PCout(execute_1_pcout));  // open: A, B, Funct30, Sa, Op, RegWriteIn, rW, PC
  ExecuteRegister executeregister_1 (
    .ALUres_in(execute_1_aluoutput), .RegWrite(execute_1_regwriteout), .rW(execute_1_rwout),
    .PC(execute_1_pcout), .Clock(Clk_out), .ALUres_out(executeregister_1_alures_out),
    .RegWriteOut(executeregister_1_regwriteout), .rWout(executeregister_1_rwout),
    .PCout(executeregister_1_pcout));
  Memory memory_1 (
    .ALUres_in(executeregister_1_alures_out), .RegWriteIn(executeregister_1_regwriteout),
    .rW(executeregister_1_rwout), .PC(executeregister_1_pcout), .ALUres_out(memory_1_alures_out),
    .RegWriteOut(memory_1_regwriteout), .rWout(memory_1_rwout), .PCout(memory_1_pcout));
  MemoryRegister memoryregister_1 (
    .ALUres_in(memory_1_alures_out), .RegWriteIn(memory_1_regwriteout), .rW(memory_1_rwout),
    .PC(memory_1_pcout), .Clock(Clk_out));  // open: ALUres_out, RegWriteOut, rWout, PCout
endmodule

module Fetch (
  input  Clock,
  output [31:0] PC,
  output [31:0] Instruction
);

  wire [31:2] incrementer_1_p2;

  Register #(.width(32)) register_1 (.D({incrementer_1_p2, PC[1:0]}), .clk(Clock), .Q(PC));  // open: en, clr
  // Incrementer #(.width(30)) incrementer_1: pin names not known; wires that end beside it: PC[31:2], incrementer_1_p2, PC
  // RISC_VProgramROM risc_vprogramrom_1: pin names not known; wires that end beside it: Instruction
endmodule

module Decode (
  input  [31:0] InstructionIn,
  input  [31:0] WriteBack,
  input  Clock,
  input  RegisterWE,
  input  [4:0] RegisterxW,
  input  [31:0] PCIn,
  output OpXOut,
  output OpMOut,
  output ALUStuffOut,
  output RegisterOut,
  output RType,
  output LUIOut,
  output UIOut,
  output [4:0] RD,
  output f3LSB,
  output [3:0] ALUOpOut,
  output [4:0] RS1,
  output [4:0] RS2,
  output [31:0] ImmExtended,
  output [19:0] ImmUType,
  output [31:0] AOut,
  output [31:0] BOut,
  output [31:0] PCOut
);

  wire not_1_out;

  // RegisterFile #(.trigger("falling")) registerfile_1: pin names not known; wires that end beside it: RegisterxW, WriteBack, Clock, RegisterWE, RegisterxW, InstructionIn[19:15], InstructionIn[24:20], AOut, BOut
  assign ImmExtended = {{20{InstructionIn[31]}}, InstructionIn[31:20]};  // Bit_Extender bit_extender_1
  and and_1 (LUIOut, InstructionIn[2], InstructionIn[5]);
  and and_2 (UIOut, InstructionIn[2], not_1_out);
  not not_1 (not_1_out, InstructionIn[5]);
  OpcodeConverter opcodeconverter_1 (
    .f3(InstructionIn[14:12]), .f7B5(InstructionIn[30]), .RType(RType), .UI(InstructionIn[2]),
    .LUI(InstructionIn[5]), .ALUOpOut(ALUOpOut));
  OpcodeDeterminer opcodedeterminer_1 (.OpCodeIn(InstructionIn[6:0]), .OpXOut(OpXOut), .OpMOut(OpMOut));
  Control control_1 (.Opcode(InstructionIn[6:0]), .ALUStuff(ALUStuffOut), .RegisterOut(RegisterOut), .RType(RType));

  assign f3LSB = InstructionIn[12];
  assign ImmUType = InstructionIn[31:12];
  assign PCOut = PCIn;
  assign RD = InstructionIn[11:7];
  assign RS1 = InstructionIn[19:15];
  assign RS2 = InstructionIn[24:20];
endmodule

module FetchRegister (
  input  [31:0] PCIn,
  input  [31:0] InstructionIn,
  input  Clock,
  output [31:0] PCOut,
  output [31:0] InstructionOut
);

  Register #(.width(32)) register_1 (.D(PCIn), .clk(Clock), .Q(PCOut));  // open: en, clr
  Register #(.width(32)) register_2 (.D(InstructionIn), .clk(Clock), .Q(InstructionOut));  // open: en, clr
endmodule

module DecodeRegister (
  input  OpXIn,
  input  OpMIn,
  input  ALUStuffIn,
  input  RegisterIn,
  input  RTypeIn,
  input  LUIIn,
  input  UIIn,
  input  [4:0] RDIn,
  input  f3LSBIn,
  input  [3:0] ALUOpIn,
  input  [4:0] RS1In,
  input  [4:0] RS2In,
  input  [31:0] ImmExtendedIn,
  input  [19:0] ImmUTypeIn,
  input  [31:0] AIn,
  input  [31:0] BIn,
  input  [31:0] PCIn,
  input  Clock,
  output OpXOut,
  output OpMOut,
  output ALUStuffOut,
  output RegisterOut,
  output RTypeOut,
  output LUIOut,
  output UIOut,
  output [4:0] RDOut,
  output f3LSBOut,
  output [3:0] ALUOpOut,
  output [4:0] RS1Out,
  output [4:0] RS2Out,
  output [31:0] ImmExtendedOut,
  output [19:0] ImmUTypeOut,
  output [31:0] AOut,
  output [31:0] BOut,
  output [31:0] PCOut
);

  Register #(.width(1)) register_1 (.D(OpXIn), .clk(Clock), .Q(OpXOut));  // open: en, clr
  Register #(.width(1)) register_2 (.D(OpMIn), .clk(Clock), .Q(OpMOut));  // open: en, clr
  Register #(.width(1)) register_3 (.D(ALUStuffIn), .clk(Clock), .Q(ALUStuffOut));  // open: en, clr
  Register #(.width(1)) register_4 (.D(RegisterIn), .clk(Clock), .Q(RegisterOut));  // open: en, clr
  Register #(.width(1)) register_5 (.D(RTypeIn), .clk(Clock), .Q(RTypeOut));  // open: en, clr
  Register #(.width(1)) register_6 (.D(LUIIn), .clk(Clock), .Q(LUIOut));  // open: en, clr
  Register #(.width(1)) register_7 (.D(UIIn), .clk(Clock), .Q(UIOut));  // open: en, clr
  Register #(.width(5)) register_8 (.D(RDIn), .clk(Clock), .Q(RDOut));  // open: en, clr
  Register #(.width(1)) register_9 (.D(f3LSBIn), .clk(Clock), .Q(f3LSBOut));  // open: en, clr
  Register #(.width(4)) register_10 (.D(ALUOpIn), .clk(Clock), .Q(ALUOpOut));  // open: en, clr
  Register #(.width(5)) register_11 (.D(RS1In), .clk(Clock), .Q(RS1Out));  // open: en, clr
  Register #(.width(5)) register_12 (.D(RS2In), .clk(Clock), .Q(RS2Out));  // open: en, clr
  Register #(.width(32)) register_13 (.D(ImmExtendedIn), .clk(Clock), .Q(ImmExtendedOut));  // open: en, clr
  Register #(.width(20)) register_14 (.D(ImmUTypeIn), .clk(Clock), .Q(ImmUTypeOut));  // open: en, clr
  Register #(.width(32)) register_15 (.D(AIn), .clk(Clock), .Q(AOut));  // open: en, clr
  Register #(.width(32)) register_16 (.D(BIn), .clk(Clock), .Q(BOut));  // open: en, clr
  Register #(.width(32)) register_17 (.D(PCIn), .clk(Clock), .Q(PCOut));  // open: en, clr
endmodule

module Execute (
  input  [31:0] A,
  input  [31:0] B,
  input  Funct30,
  input  [4:0] Sa,
  input  [3:0] Op,
  input  RegWriteIn,
  input  [4:0] rW,
  input  [31:0] PC,
  output [31:0] ALUOutput,
  output RegWriteOut,
  output [4:0] rWout,
  output [31:0] PCout
);

  wire [31:0] alu_1_p6;

  // ALU alu_1: pin names not known; wires that end beside it: Funct30, A, B, Op, Sa, alu_1_p6
  ALUresult aluresult_1 (
    .A(A), .B(B), .C(alu_1_p6), .Funct30(Funct30), .Op0(Op[0]), .Op1(Op[1]), .RegWriteIn(RegWriteIn),
    .ALUOutput(ALUOutput), .RegWriteOut(RegWriteOut));

  assign PCout = PC;
  assign rWout = rW;
endmodule

module ExecuteRegister (
  input  [31:0] ALUres_in,
  input  RegWrite,
  input  [4:0] rW,
  input  [31:0] PC,
  input  Clock,
  output [31:0] ALUres_out,
  output RegWriteOut,
  output [4:0] rWout,
  output [31:0] PCout
);

  Register #(.width(32)) register_1 (.D(ALUres_in), .clk(Clock), .Q(ALUres_out));  // open: en, clr
  Register #(.width(1)) register_2 (.D(RegWrite), .clk(Clock), .Q(RegWriteOut));  // open: en, clr
  Register #(.width(5)) register_3 (.D(rW), .clk(Clock), .Q(rWout));  // open: en, clr
  Register #(.width(32)) register_4 (.D(PC), .clk(Clock), .Q(PCout));  // open: en, clr
endmodule

module Memory (
  input  [31:0] ALUres_in,
  input  RegWriteIn,
  input  [4:0] rW,
  input  [31:0] PC,
  output [31:0] ALUres_out,
  output RegWriteOut,
  output [4:0] rWout,
  output [31:0] PCout
);


  assign ALUres_out = ALUres_in;
  assign PCout = PC;
  assign RegWriteOut = RegWriteIn;
  assign rWout = rW;
endmodule

module MemoryRegister (
  input  [31:0] ALUres_in,
  input  RegWriteIn,
  input  [4:0] rW,
  input  [31:0] PC,
  input  Clock,
  output [31:0] ALUres_out,
  output RegWriteOut,
  output [4:0] rWout,
  output [31:0] PCout
);

  Register #(.width(32)) register_1 (.D(ALUres_in), .clk(Clock), .Q(ALUres_out));  // open: en, clr
  Register #(.width(1)) register_2 (.D(RegWriteIn), .clk(Clock), .Q(RegWriteOut));  // open: en, clr
  Register #(.width(5)) register_3 (.D(rW), .clk(Clock), .Q(rWout));  // open: en, clr
  Register #(.width(32)) register_4 (.D(PC), .clk(Clock), .Q(PCout));  // open: en, clr
endmodule

module Control (
  input  [6:0] Opcode,
  output ALUStuff,
  output RegisterOut,
  output RType
);

  wire not_1_out, not_2_out, not_3_out;

  not not_1 (not_1_out, Opcode[0]);
  Multiplexer #(.select(2), .enable("false")) multiplexer_1 (
    .in0(Opcode[0]), .in1(Opcode[0]), .in2(not_1_out), .in3(Opcode[0]), .out(ALUStuff),
    .sel({Opcode[5], Opcode[2]}));
  not not_2 (not_2_out, Opcode[0]);
  Multiplexer #(.select(2), .enable("false")) multiplexer_2 (
    .in0(Opcode[0]), .in1(not_2_out), .in2(Opcode[0]), .in3(Opcode[0]), .sel({Opcode[5], Opcode[2]}));  // open: out
  not not_3 (not_3_out, Opcode[2]);
  and and_1 (RType, not_3_out, Opcode[5]);

  assign RegisterOut = Opcode[4];
endmodule

module OpcodeConverter (
  input  [2:0] f3,
  input  f7B5,
  input  RType,
  input  UI,
  input  LUI,
  output [3:0] ALUOpOut
);

  wire and_1_out, and_2_out, and_3_out, and_4_out, and_5_out, and_6_out, and_7_out, and_8_out, and_9_out,
       and_10_out, not_1_out, not_2_out, not_3_out, not_4_out, not_5_out, not_6_out, not_7_out, not_8_out,
       not_9_out, not_10_out, not_11_out;
  wire [2:0] not_13_out;
  wire [2:2] not_14_out;
  wire [3:0] multiplexer_1_out, or_4_out;

  not not_1 (not_1_out, f3[2]);
  and and_1 (and_1_out, not_1_out, not_2_out);
  not not_2 (not_2_out, f3[1]);
  not not_3 (not_3_out, f3[1]);
  and and_2 (and_2_out, not_3_out, f3[0]);
  and and_3 (and_3_out, f3[0], not_4_out);
  not not_4 (not_4_out, f3[1]);
  and and_4 (and_4_out, f3[0], f3[2]);
  and and_5 (and_5_out, f3[2], not_5_out);
  not not_5 (not_5_out, f3[1]);
  not not_6 (not_6_out, f3[1]);
  and and_6 (and_6_out, not_6_out, f3[2]);
  not not_7 (not_7_out, f3[0]);
  and and_7 (and_7_out, f7B5, not_7_out, not_8_out, RType);
  not not_8 (not_8_out, f3[1]);
  and and_8 (and_8_out, f7B5, not_9_out);
  not not_9 (not_9_out, f3[1]);
  not not_10 (not_10_out, f3[1]);
  and and_9 (and_9_out, not_10_out, not_11_out);
  not not_11 (not_11_out, f3[0]);
  and and_10 (and_10_out, f3[2], f3[1]);
  or or_1 (or_4_out[3], and_1_out, and_2_out);
  or or_2 (or_4_out[1], and_3_out, and_4_out, and_5_out);
  or or_3 (or_4_out[2], and_6_out, and_7_out);
  or or_4 (or_4_out[0], and_8_out, and_9_out, and_10_out);
  not not_12 (not_13_out[2], LUI);
  not not_13 (not_13_out[0], LUI);
  not not_14 (not_14_out[2], UI);
  Multiplexer #(.width(4), .enable("false")) multiplexer_1 (
    .in0({UI, {2{not_14_out[2]}}, UI}), .in1({LUI, not_13_out[2], LUI, not_13_out[0]}),
    .out(multiplexer_1_out), .sel(LUI));
  Multiplexer #(.width(4), .enable("false")) multiplexer_2 (
    .in0(or_4_out), .in1(multiplexer_1_out), .out(ALUOpOut), .sel(UI));
endmodule

module OpcodeDeterminer (
  input  [6:0] OpCodeIn,
  output OpXOut,
  output OpMOut
);

  wire nor_1_out;

  nor nor_1 (nor_1_out, OpCodeIn[6], OpCodeIn[5], OpCodeIn[4], OpCodeIn[3], OpCodeIn[2]);
  and and_1 (OpMOut, nor_1_out, OpCodeIn[1], OpCodeIn[0]);
  not not_1 (OpXOut, OpMOut);
endmodule

module ALUresult (
  input  [31:0] A,
  input  [31:0] B,
  input  [31:0] C,
  input  Funct30,
  input  Op0,
  input  Op1,
  input  RegWriteIn,
  output [31:0] ALUOutput,
  output RegWriteOut
);

  wire comparator_1_lt, comparator_2_lt;
  wire [31:0] bit_extender_1_out, bit_extender_2_out, multiplexer_1_out, multiplexer_2_out;

  Comparator #(.width(32)) comparator_1 (.a(A), .b(B), .lt(comparator_1_lt));  // open: gt, eq
  Comparator #(.width(32), .mode("unsigned")) comparator_2 (.a(A), .b(B), .lt(comparator_2_lt));  // open: gt, eq
  assign bit_extender_1_out = {{31{1'b0}}, comparator_1_lt};  // Bit_Extender bit_extender_1
  assign bit_extender_2_out = {{31{1'b0}}, comparator_2_lt};  // Bit_Extender bit_extender_2
  Multiplexer #(.width(32), .enable("false")) multiplexer_1 (
    .in0(bit_extender_1_out), .in1(bit_extender_2_out), .out(multiplexer_1_out), .sel(Funct30));
  Multiplexer #(.width(32), .enable("false")) multiplexer_2 (
    .in0(multiplexer_1_out), .in1(C), .out(multiplexer_2_out), .sel(Op0));
  Multiplexer #(.width(32), .enable("false")) multiplexer_3 (
    .in0(multiplexer_2_out), .in1(C), .out(ALUOutput), .sel(Op1));

  assign RegWriteOut = RegWriteIn;
endmodule
